// Digital circuit CPU_v1.dig as structural Verilog
module CPU_v1 (
  input  clk,
  input  En,
  input  Clr,
  output [7:0] out_4
);

  wire A_in, A_out, ALU_0, ALU_1, ALU_2, ALU_out, B_in, Cp, Ep, Halt, NCE, NEi, NLi, NLm, OUT_in, PC_in,
       RAM_out;
  wire [3:0] inputmar_1_out, ir_1_q, OpCode;
  wire [7:0] pc_1_pc, rom_1_d;
  wire [16:16] register_1_q;
  wire [17:0] controller_certo_1_out;

  controller_certo controller_certo_1 (
    .Clk(clk), .In(clk), .En(En), .OpCode(OpCode), .Clr(Clr), .Out(controller_certo_1_out));
  Register #(.Bits(18)) register_1 (
    .D(controller_certo_1_out), .C(clk), .en(En),
    .Q({Halt, register_1_q[16], OUT_in, ALU_out, ALU_2, ALU_1, ALU_0, B_in, A_out, NCE, NLm, PC_in, Cp, Ep, NEi, NLi, RAM_out, A_in}));
  ir ir_1 (.NLi(out_4), .Clk(clk), .Clr(Clr), .NEi(NEi), .Q({OpCode, ir_1_q}));
  pc pc_1 (.Cp(Cp), .Clk(clk), .Clr(Clr), .Ep(Ep), .Bus(out_4), .Pc(pc_1_pc));
  InputMAR inputmar_1 (.NLm(NLm), .Bus(out_4[3:0]), .Clk(clk), .Out(inputmar_1_out));
  ROM #(.AddrBits(8), .isProgramMemory("true"), .Bits(8)) rom_1 (
    .A({4'b0000, inputmar_1_out}), .sel(RAM_out), .D(rom_1_d));
  assign out_4 = Ep ? pc_1_pc : 8'bz;  // Driver driver_1
  assign out_4 = RAM_out ? rom_1_d : 8'bz;  // Driver driver_2
  assign out_4 = NEi ? {4'b0000, ir_1_q} : 8'bz;  // Driver driver_3

  // Other names for the same wires on the sheet: Bus_in[7:0] = out_4; Bus_out[7:0] = out_4

  // Notes on the sheet:
  //   Bit	Sinal
  //   17 -> HALT	
  //   16 -> RESET_T
  //   15 ->OUT_in
  //   14 -> ALU_out	
  //   13 -> ALU_Sel2	
  //   12 ->ALU_Sel1
  //   11-> ALU_Sel0	
  //   10 -> B_in	
  //   9 -> A_out	
  //   8 -> NCE
  //   7 -> NLm
  //   6 - > PC_in
  //   5 -> Cp
  //   4 -> Ep
  //   3 -> NEi
  //   2 -> NLi
  //   1 -> RAM_out
  //   0 -> A_in
endmodule
