// Digital circuit InputMAR.dig as structural Verilog
module InputMAR (
  input  NLm,
  input  [3:0] Bus,
  input  Clk,
  output [3:0] Out
);

  wire B0, B1, B2, B3, Lm;

  not not_1 (Lm, NLm);
  assign {B3, B2, B1, B0} = Lm ? Bus : 4'bz;  // Driver driver_1
  D_FF d_ff_1 (.D(B0), .C(Clk), .Q(Out[0]));  // open: nQ
  D_FF d_ff_2 (.D(B1), .C(Clk), .Q(Out[1]));  // open: nQ
  D_FF d_ff_3 (.D(B2), .C(Clk), .Q(Out[2]));  // open: nQ
  D_FF d_ff_4 (.D(B3), .C(Clk), .Q(Out[3]));  // open: nQ

  // Other names for the same wires on the sheet: R0 = Out[0]; R1 = Out[1]; R2 = Out[2]; R3 = Out[3]
endmodule
