// Digital circuit add8.dig as structural Verilog
module add8 (
  input  [7:0] A,
  input  [7:0] B,
  output [7:0] S,
  output Count
);

  wire Cout1, Cout2, Cout3, Cout4, Cout5, Cout6, Cout7;

  add add_1 (.A(A[0]), .B(B[0]), .Cin(1'b0), .S(S[0]), .Cout(Cout1));
  add add_2 (.A(A[1]), .B(B[1]), .Cin(Cout1), .S(S[1]), .Cout(Cout2));
  add add_3 (.A(A[2]), .B(B[2]), .Cin(Cout2), .S(S[2]), .Cout(Cout3));
  add add_4 (.A(A[3]), .B(B[3]), .Cin(Cout3), .S(S[3]), .Cout(Cout4));
  add add_5 (.A(A[4]), .B(B[4]), .Cin(Cout4), .S(S[4]), .Cout(Cout5));
  add add_6 (.A(A[5]), .B(B[5]), .Cin(Cout5), .S(S[5]), .Cout(Cout6));
  add add_7 (.A(A[6]), .B(B[6]), .Cin(Cout6), .S(S[6]), .Cout(Cout7));
  add add_8 (.A(A[7]), .B(B[7]), .Cin(Cout7), .S(S[7]), .Cout(Count));

  // Other names for the same wires on the sheet: dA0 = A[0]; dA1 = A[1]; dA2 = A[2]; dA3 = A[3]; dA4 = A[4];
  //   dA5 = A[5]; dA6 = A[6]; dA7 = A[7]; dB0 = B[0]; dB1 = B[1]; dB2 = B[2]; dB3 = B[3]; dB4 = B[4]; dB5 = B[5];
  //   dB6 = B[6]; dB7 = B[7]; dS0 = S[0]; dS1 = S[1]; dS2 = S[2]; dS3 = S[3]; dS4 = S[4]; dS5 = S[5]; dS6 = S[6];
  //   dS7 = S[7]
endmodule
