// Digital circuit controller_certo.dig as structural Verilog
module controller_certo (
  input  Clk,
  input  In,
  input  En,
  input  [3:0] OpCode,
  input  Clr,
  output [17:0] Out
);

  wire _0, _1, _2, _3, _4, _5, _6, and_1_out, and_2_out;
  wire [2:0] counter_1_out;
  wire [17:0] multiplexer_1_out, multiplexer_2_out, multiplexer_3_out, multiplexer_4_out;

  Counter #(.Bits(3), .isProgramCounter("true")) counter_1 (
    .en(En), .C(In), .clr(and_1_out), .out(counter_1_out));  // open: ovf
  and and_1 (and_1_out, counter_1_out[1], counter_1_out[2]);
  and and_2 (and_2_out, En, ~counter_1_out[0], ~counter_1_out[1], ~counter_1_out[2]);  // And
  ring_counter ring_counter_1 (.Clk(Clk), .In(and_2_out), .Clr(Clr), .Out({_6, _5, _4, _3, _2, _1, _0}));
  Multiplexer #(.Selector_Bits(4), .Bits(18)) multiplexer_1 (
    .sel(OpCode), .in_0(18'h10000), .in_1(18'h88), .in_2(18'h88), .in_3(18'h88), .in_4(18'h88),
    .in_5(18'h5201), .in_6(18'h5a01), .in_7(18'h48), .in_8(18'h48), .in_9(18'h8200), .in_10(18'h20000),
    .in_11({18{1'b0}}), .in_12({18{1'b0}}), .in_13({18{1'b0}}), .in_14({18{1'b0}}), .in_15({18{1'b0}}),
    .out(multiplexer_1_out));
  Multiplexer #(.Selector_Bits(4), .Bits(18)) multiplexer_2 (
    .sel(OpCode), .in_0({18{1'b0}}), .in_1(18'h3), .in_2(18'h300), .in_3(18'h402), .in_4(18'h402),
    .in_5(18'h10000), .in_6(18'h10000), .in_7(18'h10000), .in_8(18'h10000), .in_9(18'h10000),
    .in_10({18{1'b0}}), .in_11({18{1'b0}}), .in_12({18{1'b0}}), .in_13({18{1'b0}}), .in_14({18{1'b0}}),
    .in_15({18{1'b0}}), .out(multiplexer_2_out));
  Multiplexer #(.Selector_Bits(4), .Bits(18)) multiplexer_3 (
    .sel(OpCode), .in_0({18{1'b0}}), .in_1({18{1'b0}}), .in_2(18'h10000), .in_3(18'h10000), .in_4(18'h4201),
    .in_5(18'h4a01), .in_6({18{1'b0}}), .in_7({18{1'b0}}), .in_8({18{1'b0}}), .in_9({18{1'b0}}),
    .in_10({18{1'b0}}), .in_11({18{1'b0}}), .in_12({18{1'b0}}), .in_13({18{1'b0}}), .in_14({18{1'b0}}),
    .in_15({18{1'b0}}), .out(multiplexer_3_out));
  Multiplexer #(.Selector_Bits(4), .Bits(18)) multiplexer_4 (
    .sel(OpCode), .in_0({18{1'b0}}), .in_1({18{1'b0}}), .in_2({18{1'b0}}), .in_3(18'h10000),
    .in_4(18'h10000), .in_5({18{1'b0}}), .in_6({18{1'b0}}), .in_7({18{1'b0}}), .in_8({18{1'b0}}),
    .in_9({18{1'b0}}), .in_10({18{1'b0}}), .in_11({18{1'b0}}), .in_12({18{1'b0}}), .in_13({18{1'b0}}),
    .in_14({18{1'b0}}), .in_15({18{1'b0}}), .out(multiplexer_4_out));
  assign Out = _4 ? multiplexer_2_out : 18'bz;  // Driver driver_1
  assign Out = _5 ? multiplexer_3_out : 18'bz;  // Driver driver_2
  assign Out = _0 ? 18'h90 : 18'bz;  // Driver driver_3
  assign Out = _1 ? 18'h20 : 18'bz;  // Driver driver_4
  assign Out = _2 ? 18'h6 : 18'bz;  // Driver driver_5
  assign Out = _3 ? multiplexer_1_out : 18'bz;  // Driver driver_6
  assign Out = _6 ? multiplexer_4_out : 18'bz;  // Driver driver_7
endmodule
