// Digital circuit decremento8bits.dig as structural Verilog
module decremento8bits (
  input  [7:0] In,
  output [7:0] Out
);

  wire subtrator8bits_1_neg;

  subtrator8bits subtrator8bits_1 (.A(In), .B(8'h1), .Neg(subtrator8bits_1_neg), .Out(Out));
  LED led_1 (.in(subtrator8bits_1_neg));
endmodule
