// Digital circuit divisor4bits.dig as structural Verilog
module divisor4bits (
  input  [3:0] D,
  input  [3:0] d_2,
  output [3:0] q,
  output [3:0] r
);

  wire nq0, nq1, nq2, nq3;
  wire [3:0] multiplexer_1_out, multiplexer_2_out, multiplexer_3_out, op0, op1, op2, op3, r0, r1, r2, r3;

  not not_1 (q[0], nq0);
  not not_2 (q[1], nq1);
  not not_3 (q[2], nq2);
  not not_4 (q[3], nq3);
  Multiplexer #(.Bits(4)) multiplexer_1 (.sel(nq3), .in_0(r3), .in_1(op3), .out(multiplexer_1_out));
  Multiplexer #(.Bits(4)) multiplexer_2 (.sel(nq2), .in_0(r2), .in_1(op2), .out(multiplexer_2_out));
  Multiplexer #(.Bits(4)) multiplexer_3 (.sel(nq1), .in_0(r1), .in_1(op1), .out(multiplexer_3_out));
  shift shift_1 (.In(4'b0000), .Shft(D[3]), .S(op3));
  shift shift_2 (.In(multiplexer_1_out), .Shft(D[2]), .S(op2));
  shift shift_3 (.In(multiplexer_2_out), .Shft(D[1]), .S(op1));
  shift shift_4 (.In(multiplexer_3_out), .Shft(D[0]), .S(op0));
  Multiplexer #(.Bits(4)) multiplexer_4 (.sel(nq0), .in_0(r0), .in_1(op0), .out(r));
  Sub #(.Bits(4)) sub_1 (.a(op3), .b(d_2), .c_i(1'b0), .s(r3), .c_o(nq3));
  Sub #(.Bits(4)) sub_2 (.a(op2), .b(d_2), .c_i(1'b0), .s(r2), .c_o(nq2));
  Sub #(.Bits(4)) sub_3 (.a(op1), .b(d_2), .c_i(1'b0), .s(r1), .c_o(nq1));
  Sub #(.Bits(4)) sub_4 (.a(op0), .b(d_2), .c_i(1'b0), .s(r0), .c_o(nq0));

  // Other names for the same wires on the sheet: d_t[3:0] = d_2
endmodule
