// Digital circuit full_adder.dig as structural Verilog
module full_adder (
  input  A,
  input  B,
  input  Ci,
  output S,
  output Carry_Out
);

  wire CoA_out, CoB_out, half_adder_1_s;

  half_adder half_adder_1 (.A(A), .B(B), .S(half_adder_1_s), .Carry_Out(CoA_out));
  or or_1 (Carry_Out, CoA_out, CoB_out);
  half_adder half_adder_2 (.A(half_adder_1_s), .B(Ci), .S(S), .Carry_Out(CoB_out));

  // Other names for the same wires on the sheet: A_Out = A; B_Out = B; Ci_Out = Ci; Co_Out = Carry_Out; S_Out = S
endmodule
