// Digital circuit half-adder.dig as structural Verilog
module half_adder (
  input  A,
  input  B,
  output S,
  output Carry_Out
);

  xor xor_1 (S, A, B);
  and and_1 (Carry_Out, A, B);

  // Other names for the same wires on the sheet: AND_Out = Carry_Out; XOR_Out = S
endmodule
