// Digital circuit incremento8bits.dig as structural Verilog
module incremento8bits (
  input  [7:0] In,
  output [7:0] Out
);

  // add8 add8_1: pin names not known; wires that end beside it: In, 8'h1, Out
endmodule
