// Digital circuit mem.dig as structural Verilog
module mem (
  input  [7:0] Bus_in,
  input  MAR_LD,
  input  CLK,
  input  Clr,
  output [7:0] Out
);

  wire [7:0] MAR_q;

  Register #(.Bits(8)) MAR (.D(Bus_in), .C(CLK), .en(MAR_LD), .Q(MAR_q));
  ROM #(.AddrBits(8), .Bits(8)) rom_1 (.A(MAR_q), .sel(1'b1), .D(Out));

  // Notes on the sheet:
  //   contents of rom_1 (hex, n*v repeats v):
  //   1f,3e,70,e0,97,82,0,f0,6*0,4,7,3e,0,0,700,e00,11*0,70,207*0,3
endmodule
