// Digital circuit multiplier2.dig as structural Verilog
module multiplier2 (
  input  [3:0] A,
  input  [3:0] B,
  output [7:0] S
);

  wire C_3A, C_3B, C_4A, C_4B, C_out_1, C_out_2, C_out_3, C_out_4, C_out_5, C_outH_2, C_partial_2a, S01, S02,
       S03, S10, S11, S12, S13, S20, S21, S22, S23, S30, S31, S32, S33, S_3A, S_4A, S_partial_2;

  and and_1 (S[0], A[0], B[0]);
  and and_2 (S10, A[1], B[0]);
  and and_3 (S20, A[2], B[0]);
  and and_4 (S30, A[3], B[0]);
  full_adder fa_5a (.A(S32), .B(S23), .Ci(C_out_4), .S(S[5]), .Carry_Out(C_out_5));
  half_adder ha_6a (.A(S33), .B(C_out_5), .S(S[6]), .Carry_Out(S[7]));
  and and_5 (S01, A[0], B[1]);
  and and_6 (S11, A[1], B[1]);
  and and_7 (S21, A[2], B[1]);
  and and_8 (S31, A[3], B[1]);
  full_adder fa_4a (.A(S31), .B(S22), .Ci(S13), .S(S_4A), .Carry_Out(C_4A));
  half_adder ha_4a (.A(S_4A), .B(C_out_3), .S(S[4]), .Carry_Out(C_4B));
  or or_1 (C_out_4, C_4A, C_4B);
  and and_9 (S02, A[0], B[2]);
  and and_10 (S12, A[1], B[2]);
  and and_11 (S22, A[2], B[2]);
  and and_12 (S32, A[3], B[2]);
  full_adder fa_3a (.A(S30), .B(S21), .Ci(S12), .S(S_3A), .Carry_Out(C_3A));
  full_adder fa_3b (.A(S_3A), .B(S03), .Ci(C_out_2), .S(S[3]), .Carry_Out(C_3B));
  or or_2 (C_out_3, C_3A, C_3B);
  and and_13 (S03, A[0], B[3]);
  and and_14 (S13, A[1], B[3]);
  and and_15 (S23, A[2], B[3]);
  and and_16 (S33, A[3], B[3]);
  half_adder half_adder_1 (.A(S10), .B(S01), .S(S[1]), .Carry_Out(C_out_1));
  full_adder full_adder_1 (.A(S20), .B(S11), .Ci(C_out_1), .S(S_partial_2), .Carry_Out(C_partial_2a));
  half_adder half_adder_2 (.A(S_partial_2), .B(S02), .S(S[2]), .Carry_Out(C_outH_2));
  or or_3 (C_out_2, C_partial_2a, C_outH_2);

  // Other names for the same wires on the sheet: C_out_6 = S[7]; S00 = S[0]
endmodule
