// Digital circuit pc.dig as structural Verilog
module pc (
  input  Cp,
  input  Clk,
  input  Clr,
  input  Ep,
  input  [7:0] Bus,
  output [7:0] Pc
);

  CounterPreset #(.Bits(8)) counterpreset_1 (
    .en(Ep), .C(Clk), .dir(1'b0), .in(Bus), .ld(Cp), .clr(Clr), .out(Pc));  // open: ovf
endmodule
