// Digital circuit ring_counter.dig as structural Verilog
module ring_counter (
  input  Clk,
  input  In,
  input  Clr,
  output [6:0] Out
);

  D_FF_AS d_ff_as_1 (.Set(1'b0), .D(In), .C(Clk), .Clr(Clr), .Q(Out[0]));  // open: nQ
  D_FF_AS d_ff_as_2 (.Set(1'b0), .D(Out[0]), .C(Clk), .Clr(Clr), .Q(Out[1]));  // open: nQ
  D_FF_AS d_ff_as_3 (.Set(1'b0), .D(Out[1]), .C(Clk), .Clr(Clr), .Q(Out[2]));  // open: nQ
  D_FF_AS d_ff_as_4 (.Set(1'b0), .D(Out[2]), .C(Clk), .Clr(Clr), .Q(Out[3]));  // open: nQ
  D_FF_AS d_ff_as_5 (.Set(1'b0), .D(Out[3]), .C(Clk), .Clr(Clr), .Q(Out[4]));  // open: nQ
  D_FF_AS d_ff_as_6 (.Set(1'b0), .D(Out[4]), .C(Clk), .Clr(Clr), .Q(Out[5]));  // open: nQ
  D_FF_AS d_ff_as_7 (.Set(1'b0), .D(Out[5]), .C(Clk), .Clr(Clr), .Q(Out[6]));  // open: nQ

  // Other names for the same wires on the sheet: Q0 = Out[0]; Q1 = Out[1]; Q2 = Out[2]; Q3 = Out[3]; Q4 = Out[4];
  //   Q5 = Out[5]; Q6 = Out[6]
endmodule
