// Digital circuit shift.dig as structural Verilog
module shift (
  input  [3:0] In,
  input  Shft,
  output [3:0] S
);


  assign S = {In[2:0], Shft};

  // Other names for the same wires on the sheet: shift = Shft
endmodule
