// Digital circuit subtrator8bits.dig as structural Verilog
module subtrator8bits (
  input  [7:0] A,
  input  [7:0] B,
  output Neg,
  output [7:0] Out
);

  wire add8_1_count;
  wire [6:0] add8_2_s;
  wire [7:0] add8_1_s, add8_3_s, not_1_out, not_2_out;

  assign not_1_out = ~B;  // Not not_1, 8 bits wide
  add8 add8_1 (.A(not_1_out), .B(8'h1), .S(add8_1_s), .Count(add8_1_count));
  LED led_1 (.in(add8_1_count));
  add8 add8_2 (.A(A), .B(add8_1_s), .S({Neg, add8_2_s}));  // open: Count
  assign not_2_out = ~{Neg, add8_2_s};  // Not not_2, 8 bits wide
  add8 add8_3 (.A(not_2_out), .B(8'h1), .S(add8_3_s));  // open: Count
  assign Out = Neg ? add8_3_s : 8'bz;  // Driver driver_1
  assign Out = ~Neg ? {Neg, add8_2_s} : 8'bz;  // DriverInvSel driverinvsel_1
endmodule
